# Fritzing sketch Gate Opener Controller Circuit (saved by Fritzing 0.9.3b)
circuit board: 3.04cm x 2.79cm
breadboards: 1

parts:
  Q1 = NPN-Transistor [package="TO92 [THT]"]
  R1 = Resistor [tolerance=±5% resistance=1k package=THT]
  D1 = Rectifier Diode [part_number=1N4001 package="300 mil [THT]"]
  C1 = Electrolytic Capacitor [capacitance=4.7µF voltage=6.3V package="100 mil [THT, electrolytic]"]
  Relay1 = SPST SIP Relay [part_number=9007-05-01 package=SIP]
  C2 = Electrolytic Capacitor [capacitance=2.2µF package="100 mil [THT, electrolytic]"]
  IC1 = DC-DC Converter [part_number=PDSE1-S package=SIP]
  Relay = female pin header, 1 pin [form="♀ (female)"]
  Relay_2 = female pin header, 1 pin [form="♀ (female)"]
  GND = female pin header, 1 pin [form="♀ (female)"]
  12V = female pin header, 1 pin [form="♀ (female)"]
  5V = female pin header, 1 pin [form="♀ (female)"]
  GND_2 = female pin header, 1 pin [form="♀ (female)"]
  GPIO = female pin header, 1 pin [form="♀ (female)"]

nets:
  GND: Q1.E, C1.-, IC1.pin1, GND_2.pin1
  N1: Q1.B, R1.Pin_1
  N2: Q1.C, D1.anode, Relay1.pin3
  N3: R1.Pin_0, GPIO.pin1
  N4: D1.cathode, C1.+, Relay1.pin2, IC1.pin2, 5V.pin1
  N5: Relay1.pin1, Relay_2.pin1
  N6: Relay1.pin4, Relay.pin1
  N7: C2.-, IC1.pin3, GND.pin1
  N8: C2.+, IC1.pin4, 12V.pin1

notes:
  Ver 2.0.0
  github.com/jgillula/rpi-gate-opener

custom parts:
  SPST SIP Relay: SIP SPST-NO Reed Relay Coto 9007-05-01
  DC-DC Converter: DC-DC Converter CUI PDSE1-S
